// Logisim project CPU.circ as structural Verilog: 6 circuits, main circuit main
module main (
);

  wire ALU_carry_out, and_1_out, and_2_out, bit_extender_2_out, CARRY_q, clock_1_out,
       controlled_buffer_2_out, controlled_inverter_1_out, controllunit_1_acc_load_from_alu,
       controllunit_1_alu_inuttype, controllunit_1_alu_optype, controllunit_1_clracc, controllunit_1_clrpc,
       controllunit_1_dectos, controllunit_1_flagen, controllunit_1_halt, controllunit_1_incpc,
       controllunit_1_inctos, controllunit_1_load_carry, controllunit_1_loadenable, controllunit_1_sc__0,
       decoder_1_out0, decoder_1_out1, decoder_1_out2, decoder_1_out3, decoder_1_out4, decoder_1_out5,
       decoder_1_out6, decoder_1_out7, decoder_1_out8, decoder_1_out9, decoder_1_out10, decoder_1_out11,
       decoder_1_out12, decoder_1_out13, decoder_1_out14, decoder_1_out15, decoder_1_out16, decoder_1_out17,
       decoder_1_out18, decoder_1_out19, decoder_1_out20, decoder_1_out21, decoder_1_out22, decoder_1_out23,
       decoder_1_out24, decoder_1_out25, decoder_1_out26, decoder_1_out27, decoder_1_out28, decoder_1_out29,
       decoder_1_out30, decoder_1_out31, decoder_2_out0, decoder_2_out1, decoder_2_out2, decoder_2_out3,
       decoder_2_out4, decoder_2_out5, decoder_2_out6, decoder_2_out7, decoder_2_out8, decoder_2_out9,
       decoder_2_out10, decoder_2_out11, decoder_2_out12, decoder_2_out13, decoder_2_out14, decoder_2_out15,
       decoder_3_out0, decoder_3_out1, decoder_3_out2, decoder_3_out3, decoder_3_out4, decoder_3_out5,
       FLAG_q, multiplexer_1_out, not_1_out, not_2_out, not_3_out, not_4_out, or_1_out, Reset_out;
  wire [1:0] controllunit_1_flagval;
  wire [2:0] controllunit_1_alu, controllunit_1_loadbus;
  wire [3:0] controllunit_1_outbus, counter_1_q;
  wire [9:0] bit_extender_1_out;
  wire [15:0] ACC_q, ALU_output, AR_q, bit_extender_3_out, bit_extender_4_out, controlled_buffer_1_out, DR_q,
       IR_q, multiplexer_2_out, PC_q, ram_1_data, TOSS_q;

  not not_1 (not_1_out, controllunit_1_halt);
  Counter #(.width(4), .max('hf)) counter_1 (
    .count(not_1_out), .Q(counter_1_q), .clk(clock_1_out), .clr(or_1_out));  // open: load, D, carry
  or or_1 (or_1_out, Reset_out, controllunit_1_halt, and_2_out);
  Decoder #(.select(5), .enable("false")) decoder_1 (
    .out0(decoder_1_out0), .out1(decoder_1_out1), .out2(decoder_1_out2), .out3(decoder_1_out3),
    .out4(decoder_1_out4), .out5(decoder_1_out5), .out6(decoder_1_out6), .out7(decoder_1_out7),
    .out8(decoder_1_out8), .out9(decoder_1_out9), .out10(decoder_1_out10), .out11(decoder_1_out11),
    .out12(decoder_1_out12), .out13(decoder_1_out13), .out14(decoder_1_out14), .out15(decoder_1_out15),
    .out16(decoder_1_out16), .out17(decoder_1_out17), .out18(decoder_1_out18), .out19(decoder_1_out19),
    .out20(decoder_1_out20), .out21(decoder_1_out21), .out22(decoder_1_out22), .out23(decoder_1_out23),
    .out24(decoder_1_out24), .out25(decoder_1_out25), .out26(decoder_1_out26), .out27(decoder_1_out27),
    .out28(decoder_1_out28), .out29(decoder_1_out29), .out30(decoder_1_out30), .out31(decoder_1_out31),
    .sel(IR_q[14:10]));
  Decoder #(.select(4)) decoder_2 (
    .out0(decoder_2_out0), .out1(decoder_2_out1), .out2(decoder_2_out2), .out3(decoder_2_out3),
    .out4(decoder_2_out4), .out5(decoder_2_out5), .out6(decoder_2_out6), .out7(decoder_2_out7),
    .out8(decoder_2_out8), .out9(decoder_2_out9), .out10(decoder_2_out10), .out11(decoder_2_out11),
    .out12(decoder_2_out12), .out13(decoder_2_out13), .out14(decoder_2_out14), .out15(decoder_2_out15),
    .sel(counter_1_q));  // open: en
  ControllUnit controllunit_1 (
    .Opcode1(decoder_1_out0), .Opcode2(decoder_1_out1), .Opcode3(decoder_1_out2), .Opcode4(decoder_1_out3),
    .Opcode5(decoder_1_out4), .Opcode6(decoder_1_out5), .Opcode7(decoder_1_out6), .Opcode8(decoder_1_out7),
    .Opcode9(decoder_1_out8), .Opcode10(decoder_1_out9), .Opcode11(decoder_1_out10),
    .Opcode12(decoder_1_out11), .Opcode13(decoder_1_out12), .Opcode14(decoder_1_out13),
    .Opcode15(decoder_1_out14), .Opcode16(decoder_1_out15), .Opcode17(decoder_1_out16),
    .Opcode18(decoder_1_out17), .Opcode19(decoder_1_out18), .Opcode20(decoder_1_out19),
    .Opcode21(decoder_1_out20), .Opcode22(decoder_1_out21), .Opcode23(decoder_1_out22),
    .Opcode24(decoder_1_out23), .Opcode25(decoder_1_out24), .Opcode26(decoder_1_out25),
    .Opcode27(decoder_1_out26), .Opcode28(decoder_1_out27), .Opcode29(decoder_1_out28),
    .Opcode30(decoder_1_out29), .Opcode31(decoder_1_out30), .Opcode32(decoder_1_out31), .T0(decoder_2_out0),
    .T1(decoder_2_out1), .T2(decoder_2_out2), .T3(decoder_2_out3), .T4(decoder_2_out4), .T5(decoder_2_out5),
    .T6(decoder_2_out6), .T7(decoder_2_out7), .T8(decoder_2_out8), .T9(decoder_2_out9),
    .T10(decoder_2_out10), .T11(decoder_2_out11), .T12(decoder_2_out12), .T13(decoder_2_out13),
    .T14(decoder_2_out14), .T15(decoder_2_out15), .I(IR_q[15]), .AR0(IR_q[0]), .AR1(IR_q[1]), .AR2(IR_q[2]),
    .AR3(IR_q[3]), .AR4(IR_q[4]), .AR5(IR_q[5]), .AR6(IR_q[6]), .AR7(IR_q[7]), .AR8(IR_q[8]), .AR9(IR_q[9]),
    .ALU_OPTYPE(controllunit_1_alu_optype), .ALU_INUTTYPE(controllunit_1_alu_inuttype),
    .ALU(controllunit_1_alu), .OUTBUS(controllunit_1_outbus), .LOADBUS(controllunit_1_loadbus),
    .ACC_LOAD_FROM_ALU(controllunit_1_acc_load_from_alu), .INCPC(controllunit_1_incpc),
    .CLRPC(controllunit_1_clrpc), .SC__0(controllunit_1_sc__0), .LOADENABLE(controllunit_1_loadenable),
    .LOAD_CARRY(controllunit_1_load_carry), .FLAG(FLAG_q), .DECtos(controllunit_1_dectos),
    .INCtos(controllunit_1_inctos), .FLAGEN(controllunit_1_flagen), .FLAGVAL(controllunit_1_flagval),
    .CLRACC(controllunit_1_clracc), .HALT(controllunit_1_halt));
  not not_2 (not_2_out, clock_1_out);
  and and_1 (and_1_out, not_2_out, clock_1_out);
  and and_2 (and_2_out, and_1_out, controllunit_1_sc__0);
  Clock clock_1 (.out(clock_1_out));
  assign controlled_buffer_1_out = not_3_out ? multiplexer_2_out : 16'bz;  // Controlled_Buffer controlled_buffer_1
  not not_3 (not_3_out, controllunit_1_acc_load_from_alu);
  Button Reset (.out(Reset_out));
  Decoder #(.select(3), .enable("false")) decoder_3 (
    .out0(decoder_3_out0), .out1(decoder_3_out1), .out2(decoder_3_out2), .out3(decoder_3_out3),
    .out4(decoder_3_out4), .out5(decoder_3_out5), .sel(controllunit_1_loadbus));  // open: out6, out7
  Bit_Extender #(.in_width(16), .out_width(10)) bit_extender_1 (.in(AR_q), .out(bit_extender_1_out));
  assign controlled_buffer_2_out = not_4_out ? 1'b0 : 1'bz;  // Controlled_Buffer controlled_buffer_2
  not not_4 (not_4_out, controllunit_1_loadenable);
  assign controlled_buffer_1_out = controllunit_1_acc_load_from_alu ? ALU_output : 16'bz;  // Controlled_Buffer controlled_buffer_3
  assign controlled_inverter_1_out = controllunit_1_loadenable ? ~decoder_3_out0 : 1'bz;  // Controlled_Inverter controlled_inverter_1
  assign controlled_buffer_2_out = controllunit_1_loadenable ? decoder_3_out0 : 1'bz;  // Controlled_Buffer controlled_buffer_4
  Register #(.width(16)) IR (.D(multiplexer_2_out), .en(decoder_3_out1), .Q(IR_q), .clk(clock_1_out));  // open: clr
  Register #(.width(16)) AR (.D(multiplexer_2_out), .en(decoder_3_out2), .Q(AR_q), .clk(clock_1_out));  // open: clr
  Counter #(.width(16), .max('hffff)) PC (
    .load(decoder_3_out3), .D(multiplexer_2_out), .count(controllunit_1_incpc), .Q(PC_q), .clk(clock_1_out),
    .clr(controllunit_1_clrpc));  // open: carry
  Register #(.width(16)) DR (.D(multiplexer_2_out), .en(decoder_3_out4), .Q(DR_q), .clk(clock_1_out));  // open: clr
  Register #(.width(16)) ACC (
    .D(controlled_buffer_1_out), .en(decoder_3_out5), .Q(ACC_q), .clk(clock_1_out),
    .clr(controllunit_1_clracc));
  ALU ALU (
    .Input1(ACC_q), .Input2(DR_q), .Operation_Type(controllunit_1_alu_optype), .Output(ALU_output),
    .Carry_Out(ALU_carry_out), .Ctrl1(controllunit_1_alu[0]), .Ctrl2(controllunit_1_alu[1]),
    .Ctrl3(controllunit_1_alu[2]), .SingleALSelect(controllunit_1_alu_inuttype));  // open: Carry_In
  Bit_Extender #(.in_width(16), .out_width(1)) bit_extender_2 (.in(ALU_output), .out(bit_extender_2_out));
  RAM #(.addrWidth(10), .dataWidth(16), .bus("separate")) ram_1 (
    .addr(bit_extender_1_out), .din(multiplexer_2_out), .data(ram_1_data), .str(controlled_buffer_2_out),
    .clk(clock_1_out), .ld(controlled_inverter_1_out));  // open: sel, clr
  Counter #(.width(16), .max('h3ff), .ongoal("stay")) TOSS (
    .load(controllunit_1_dectos), .D(16'h3ff), .count(controllunit_1_inctos), .Q(TOSS_q), .clk(clock_1_out));  // open: carry, clr
  Register #(.width(1)) CARRY (
    .D(ALU_carry_out), .en(controllunit_1_load_carry), .Q(CARRY_q), .clk(clock_1_out));  // open: clr
  Multiplexer #(.select(2), .enable("false")) multiplexer_1 (
    .in0(1'b0), .in1(1'b1), .in2(bit_extender_2_out), .out(multiplexer_1_out), .sel(controllunit_1_flagval));  // open: in3
  Register #(.width(1)) FLAG (
    .D(multiplexer_1_out), .en(controllunit_1_flagen), .Q(FLAG_q), .clk(clock_1_out));  // open: clr
  // Probe on ALU_output
  assign bit_extender_3_out = {{15{1'b0}}, CARRY_q};  // Bit_Extender bit_extender_3
  assign bit_extender_4_out = {{15{1'b0}}, FLAG_q};  // Bit_Extender bit_extender_4
  // Probe on multiplexer_2_out
  Multiplexer #(.select(4), .width(16)) multiplexer_2 (
    .in0(ram_1_data), .in1(IR_q), .in2(AR_q), .in3(PC_q), .in4(DR_q), .in5(ACC_q), .in6(TOSS_q),
    .in7(bit_extender_3_out), .in8(bit_extender_4_out), .in9(16'h3ff), .out(multiplexer_2_out),
    .sel(controllunit_1_outbus));  // open: in10, in11, in12, in13, in14, in15, en
  // Probe on controllunit_1_outbus
endmodule

module ALU (
  input  [15:0] Input1,
  input  Carry_In,
  input  SingleALSelect,
  input  [15:0] Input2,
  input  Ctrl1,
  input  Operation_Type,
  input  Ctrl2,
  input  Ctrl3,
  output [15:0] Output,
  output Carry_Out
);

  wire [15:0] dualinputal_1_output, multiplexer_1_out, singleinputal_1_output;

  Multiplexer #(.width(16), .enable("false")) multiplexer_1 (
    .in0(Input1), .in1(Input2), .out(multiplexer_1_out), .sel(SingleALSelect));
  DualInputAL dualinputal_1 (
    .CarryIn(Carry_In), .First(Input1), .Second(Input2), .Output(dualinputal_1_output), .CarryOut(Carry_Out),
    .Ctrl1(Ctrl1), .Ctrl2(Ctrl2), .Ctrl3(Ctrl3));
  SingleInputAL singleinputal_1 (
    .Input(multiplexer_1_out), .ShiftValue(4'b0001), .OutPut(singleinputal_1_output), .Ctrl1(Ctrl1),
    .Ctrl2(Ctrl2), .Ctrl3(Ctrl3));
  // Probe on singleinputal_1_output
  // Probe on dualinputal_1_output
  Multiplexer #(.width(16)) multiplexer_2 (
    .in0(dualinputal_1_output), .in1(singleinputal_1_output), .out(Output), .sel(Operation_Type));  // open: en

  // Notes on the sheet:
  //   OP-TYPE 1 => SingleInput
  //   OP-TYPE 0 => Dual Input
endmodule

module DualInputAL (
  input  CarryIn,
  input  [15:0] First,
  input  [15:0] Second,
  input  Ctrl1,
  input  Ctrl2,
  input  Ctrl3,
  output CarryOut,
  output [15:0] Output
);

  wire adder_1_cout, subtractor_1_bout;
  wire [2:0] comparator_1_gt;
  wire [15:0] adder_1_out, and_1_out, bit_extender_1_out, multiplier_1_out, or_1_out, subtractor_1_out,
       xor_1_out;

  Adder #(.width(16)) adder_1 (.a(First), .b(Second), .out(adder_1_out), .cin(CarryIn), .cout(adder_1_cout));
  Subtractor #(.width(16)) subtractor_1 (
    .a(First), .b(Second), .out(subtractor_1_out), .bin(CarryIn), .bout(subtractor_1_bout));
  assign and_1_out = First & Second;  // AND_Gate and_1, 16 bits wide
  assign or_1_out = First | Second;  // OR_Gate or_1, 16 bits wide
  assign xor_1_out = First ^ Second;  // XOR_Gate xor_1, 16 bits wide
  Multiplier #(.width(16)) multiplier_1 (.a(First), .b(Second), .out(multiplier_1_out));  // open: cin, cout
  Comparator #(.width(16), .mode("unsigned")) comparator_1 (
    .a(First), .b(Second), .gt(comparator_1_gt[0]), .eq(comparator_1_gt[1]), .lt(comparator_1_gt[2]));
  assign bit_extender_1_out = {{13{1'b0}}, comparator_1_gt};  // Bit_Extender bit_extender_1
  Multiplexer #(.select(3), .width(16)) multiplexer_1 (
    .in0(adder_1_out), .in1(subtractor_1_out), .in2(and_1_out), .in3(or_1_out), .in4(xor_1_out),
    .in5(multiplier_1_out), .in6(bit_extender_1_out), .in7(First), .out(Output), .sel({Ctrl3, Ctrl2, Ctrl1}));  // open: en
  Multiplexer #(.select(3)) multiplexer_2 (
    .in0(adder_1_cout), .in1(subtractor_1_bout), .in2(1'b0), .in3(1'b0), .in4(1'b0), .in5(1'b0), .in6(1'b0),
    .in7(1'b0), .out(CarryOut), .sel({Ctrl3, Ctrl2, Ctrl1}));  // open: en

  // Notes on the sheet:
  //   000 => ADD 
  //   001 => SUB
  //   010 => AND 
  //   011 => OR
  //   100 => XOR
  //   101 => Compare
endmodule

module SingleInputAL (
  input  [15:0] Input,
  input  [3:0] ShiftValue,
  input  Ctrl1,
  input  Ctrl2,
  input  Ctrl3,
  output [15:0] OutPut
);

  wire [15:0] adder_1_out, negator_1_out, shifter_1_out, shifter_2_out, subtractor_1_out;

  Negator #(.width(16)) negator_1 (.in(Input), .out(negator_1_out));
  Shifter #(.width(16), .shift("lr")) shifter_1 (.in(Input), .\dist (ShiftValue), .out(shifter_1_out));
  Shifter #(.width(16)) shifter_2 (.in(Input), .\dist (ShiftValue), .out(shifter_2_out));
  Adder #(.width(16)) adder_1 (.a(Input), .b(16'h1), .out(adder_1_out));  // open: cin, cout
  Subtractor #(.width(16)) subtractor_1 (.a(Input), .b(16'h1), .out(subtractor_1_out));  // open: bin, bout
  Multiplexer #(.select(3), .width(16)) multiplexer_1 (
    .in0(negator_1_out), .in1(shifter_1_out), .in2(shifter_2_out), .in3(adder_1_out), .in4(subtractor_1_out),
    .out(OutPut), .sel({Ctrl3, Ctrl2, Ctrl1}));  // open: in5, in6, in7, en

  // Notes on the sheet:
  //   000 => 2's Complement
  //   001 => Shift Right
  //   010 => Shift Left
  //   011 => Incremet
  //   100 => Decrement
endmodule

module ControllUnit (
  input  Opcode1,
  input  Opcode2,
  input  Opcode3,
  input  Opcode4,
  input  Opcode5,
  input  Opcode6,
  input  Opcode7,
  input  Opcode8,
  input  Opcode9,
  input  Opcode10,
  input  Opcode11,
  input  Opcode12,
  input  Opcode13,
  input  Opcode14,
  input  Opcode15,
  input  Opcode16,
  input  Opcode17,
  input  Opcode18,
  input  Opcode19,
  input  Opcode20,
  input  Opcode21,
  input  Opcode22,
  input  Opcode23,
  input  Opcode24,
  input  Opcode25,
  input  Opcode26,
  input  Opcode27,
  input  Opcode28,
  input  Opcode29,
  input  Opcode30,
  input  Opcode31,
  input  Opcode32,
  input  I,
  input  FLAG,
  input  AR0,
  input  AR1,
  input  AR2,
  input  AR3,
  input  AR4,
  input  AR5,
  input  AR6,
  input  AR7,
  input  AR8,
  input  AR9,
  input  T0,
  input  T1,
  input  T2,
  input  T3,
  input  T4,
  input  T5,
  input  T6,
  input  T7,
  input  T8,
  input  T9,
  input  T10,
  input  T11,
  input  T12,
  input  T13,
  input  T14,
  input  T15,
  output [2:0] LOADBUS,
  output LOADENABLE,
  output HALT,
  output ACC_LOAD_FROM_ALU,
  output LOAD_CARRY,
  output INCPC,
  output CLRPC,
  output DECtos,
  output INCtos,
  output CLRACC,
  output [3:0] OUTBUS,
  output [2:0] ALU,
  output ALU_OPTYPE,
  output ALU_INUTTYPE,
  output SC__0,
  output [1:0] FLAGVAL,
  output FLAGEN
);

  wire ALU_ADD_2_sCOMP_out, ALU_AND_SHL_out, ALU_COMPARE_out, ALU_MULT_out, ALU_OR_INC_out, ALU_SEB_SHR_out,
       ALU_XOR_DEC_out, ALUEN_out, ALUINPTYPE_out, ALUOPTYPE_out, ALUTOACC_out, and_1_out, and_2_out,
       and_3_out, and_4_out, and_5_out, and_6_out, and_7_out, and_8_out, and_9_out, and_10_out, and_11_out,
       and_12_out, and_13_out, and_14_out, and_15_out, and_16_out, and_17_out, and_18_out, and_19_out,
       and_20_out, and_21_out, and_22_out, and_23_out, and_24_out, and_25_out, and_26_out, and_27_out,
       and_28_out, and_29_out, and_30_out, and_31_out, and_32_out, and_33_out, and_34_out, and_35_out,
       and_36_out, and_37_out, and_38_out, and_39_out, and_40_out, and_41_out, and_42_out, and_43_out,
       and_44_out, and_45_out, and_46_out, and_47_out, and_48_out, and_49_out, and_50_out, and_51_out,
       and_52_out, and_53_out, and_54_out, and_55_out, and_56_out, and_57_out, and_58_out, and_59_out,
       and_60_out, and_61_out, and_62_out, and_63_out, and_64_out, and_65_out, and_66_out, and_67_out,
       and_68_out, and_69_out, and_70_out, and_71_out, and_72_out, and_73_out, and_74_out, and_75_out,
       and_76_out, and_77_out, and_78_out, and_79_out, and_80_out, and_81_out, and_82_out, and_83_out,
       and_84_out, and_85_out, and_86_out, and_87_out, and_88_out, and_89_out, and_90_out, and_91_out,
       and_92_out, and_93_out, and_94_out, and_95_out, and_96_out, and_97_out, and_98_out, and_99_out,
       and_100_out, and_101_out, and_102_out, and_103_out, and_104_out, and_105_out, and_106_out,
       BUS_3FF_out, BUS_ACC_out, BUS_AR_out, BUS_CARRY_out, BUS_DR_out, BUS_FLAG_out, BUS_IR_out,
       BUS_MEM_out, BUS_PC_out, BUS_TOS_out, CLRACC_out, decoder_1_out0, decoder_1_out1, decoder_1_out2,
       decoder_1_out3, decoder_1_out4, decoder_1_out5, decoder_1_out6, decoder_1_out7, decoder_1_out8,
       decoder_1_out9, decoder_1_out10, decoder_1_out11, decoder_1_out13, decoder_1_out14, FFUNCT_out,
       FLAG_ALU_out, FLAG_RST_out, FLAG_SET_out, FLAGEN_2_out, FLAGEN_out, LOAD_ACC_out, LOAD_AR_out,
       LOAD_DR_out, LOAD_IR_out, LOAD_MEM_out, LOAD_PC_out, nor_1_out, not_1_out, not_2_out, not_3_out,
       not_4_out, or_1_out, or_2_out, or_3_out, or_4_out, or_5_out, or_6_out, or_7_out,
       priority_encoder_3_gs, priority_encoder_5_p2, priority_encoder_5_p3, priority_encoder_5_p4,
       priority_encoder_5_p5, priority_encoder_6_p2, priority_encoder_6_p3, priority_encoder_6_p4,
       priority_encoder_6_p5, priority_encoder_6_p6, priority_encoder_6_p7, priority_encoder_6_p8,
       priority_encoder_7_p2, priority_encoder_7_p3, priority_encoder_7_p4, priority_encoder_8_p2,
       priority_encoder_8_p3, priority_encoder_8_p4, priority_encoder_8_p5, SC__0_out;
  wire [1:0] priority_encoder_4_out, priority_encoder_7_p1;
  wire [2:0] priority_encoder_1_out, priority_encoder_3_out, priority_encoder_5_p1, priority_encoder_6_p1;
  wire [3:0] priority_encoder_2_out, priority_encoder_8_p1;

  // Probe on nothing
  not not_1 (not_1_out, FLAG);
  not not_2 (not_2_out, FLAG);
  // Probe on I
  and and_1 (and_1_out, Opcode1, T4);
  and and_2 (and_2_out, T4, Opcode2);
  and and_3 (and_3_out, Opcode3, T4);
  and and_4 (and_4_out, Opcode4, T4);
  and and_5 (and_5_out, T4, Opcode5);
  and and_6 (and_6_out, T4, Opcode6);
  and and_7 (and_7_out, Opcode7, T4);
  and and_8 (and_8_out, Opcode12, T4);
  and and_9 (and_9_out, T4, Opcode8);
  and and_10 (and_10_out, T5, Opcode7);
  and and_11 (and_11_out, Opcode1, T5);
  and and_12 (and_12_out, Opcode2, T5);
  and and_13 (and_13_out, Opcode3, T5);
  and and_14 (and_14_out, Opcode4, T5);
  and and_15 (and_15_out, T5, Opcode5);
  and and_16 (and_16_out, Opcode6, T5);
  and and_17 (and_17_out, Opcode12, T6);
  and and_18 (and_18_out, Opcode12, T7);
  and and_19 (and_19_out, Opcode9, T4);
  and and_20 (and_20_out, Opcode7, T4);
  and and_21 (and_21_out, Opcode12, T5);
  and and_22 (and_22_out, T5, Opcode1);
  and and_23 (and_23_out, Opcode7, T5);
  and and_24 (and_24_out, T5, Opcode6);
  and and_25 (and_25_out, Opcode2, T5);
  and and_26 (and_26_out, Opcode3, T5);
  and and_27 (and_27_out, Opcode4, T5);
  and and_28 (and_28_out, T5, Opcode5);
  and and_29 (and_29_out, Opcode9, T4);
  and and_30 (and_30_out, Opcode12, T6);
  and and_31 (and_31_out, T3, I);
  and and_32 (and_32_out, Opcode12, T5);
  and and_33 (and_33_out, Opcode10, T4);
  and and_34 (and_34_out, Opcode11, T4, FLAG);
  and and_35 (and_35_out, T7, Opcode12);
  and and_36 (and_36_out, Opcode13, not_1_out, T4);
  and and_37 (and_37_out, Opcode1, T5);
  and and_38 (and_38_out, T5, Opcode2);
  and and_39 (and_39_out, Opcode3, T5);
  and and_40 (and_40_out, Opcode4, T5);
  and and_41 (and_41_out, T5, Opcode5);
  and and_42 (and_42_out, T5, Opcode6);
  and and_43 (and_43_out, Opcode7, T5);
  and and_44 (and_44_out, Opcode8, T4);
  and and_45 (and_45_out, Opcode9, T4);
  and and_46 (and_46_out, Opcode10, T4);
  and and_47 (and_47_out, Opcode11, T4);
  and and_48 (and_48_out, Opcode12, T7);
  and and_49 (and_49_out, Opcode13, T4);
  and and_50 (and_50_out, T3, I);
  and and_51 (and_51_out, T4, Opcode1);
  and and_52 (and_52_out, T4, Opcode2);
  and and_53 (and_53_out, Opcode3, T4);
  and and_54 (and_54_out, Opcode4, T4);
  and and_55 (and_55_out, T4, Opcode5);
  and and_56 (and_56_out, Opcode6, T4);
  and and_57 (and_57_out, Opcode8, T4);
  and and_58 (and_58_out, Opcode10, T4);
  and and_59 (and_59_out, Opcode12, T4);
  and and_60 (and_60_out, Opcode13, not_2_out, T4);
  and and_61 (and_61_out, Opcode11, FLAG, T4);
  buf or_1 (or_1_out, 1'b0);  // OR_Gate
  buf or_2 (or_2_out, or_1_out);  // OR_Gate
  or ALU_ADD_2_sCOMP (ALU_ADD_2_sCOMP_out, and_22_out, and_23_out);
  or ALU_SEB_SHR (ALU_SEB_SHR_out, and_24_out, 1'b0);
  or ALU_AND_SHL (ALU_AND_SHL_out, 1'b0, and_25_out);
  or ALU_OR_INC (ALU_OR_INC_out, 1'b0, and_26_out);
  or ALU_XOR_DEC (ALU_XOR_DEC_out, and_27_out, 1'b0);
  or ALU_MULT (ALU_MULT_out, and_28_out, 1'b0);
  buf ALU_COMPARE (ALU_COMPARE_out, 1'b0);  // OR_Gate
  or u_SC__0 (SC__0_out, and_37_out, and_38_out, and_39_out, and_40_out, and_41_out, and_42_out, and_43_out, and_44_out, and_45_out, and_46_out, and_47_out, and_48_out, and_49_out);
  buf FLAG_SET (FLAG_SET_out, 1'b0);  // OR_Gate
  buf FLAG_RST (FLAG_RST_out, 1'b0);  // OR_Gate
  buf FLAG_ALU (FLAG_ALU_out, 1'b0);  // OR_Gate
  or ALUEN (ALUEN_out, and_10_out, and_11_out, and_12_out, and_13_out, and_14_out, and_15_out, and_16_out);
  buf BUS_IR (BUS_IR_out, and_59_out);  // OR_Gate
  or BUS_AR (BUS_AR_out, and_60_out, and_61_out);
  or BUS_PC (BUS_PC_out, T0, and_17_out);
  buf BUS_DR (BUS_DR_out, and_18_out);  // OR_Gate
  buf BUS_ACC (BUS_ACC_out, and_19_out);  // OR_Gate
  buf BUS_TOS (BUS_TOS_out, 1'b0);  // OR_Gate
  or BUS_CARRY (BUS_CARRY_out, 1'b0, and_20_out);
  buf BUS_FLAG (BUS_FLAG_out, 1'b0);  // OR_Gate
  buf BUS_3FF (BUS_3FF_out, and_21_out);  // OR_Gate
  buf or_3 (or_3_out, 1'b0);  // OR_Gate
  buf or_4 (or_4_out, 1'b0);  // OR_Gate
  or LOAD_MEM (LOAD_MEM_out, and_29_out, and_30_out);
  buf LOAD_IR (LOAD_IR_out, T1);  // OR_Gate
  or BUS_MEM (BUS_MEM_out, T1, T2, and_50_out, and_51_out, and_52_out, and_53_out, and_54_out, and_55_out, and_56_out, and_57_out, and_58_out);
  or LOAD_AR (LOAD_AR_out, T0, T2, and_31_out, and_32_out);
  or LOAD_PC (LOAD_PC_out, and_33_out, and_34_out, and_35_out, and_36_out);
  or LOAD_DR (LOAD_DR_out, and_1_out, and_2_out, and_3_out, and_4_out, and_5_out, and_6_out, and_7_out, and_8_out);
  or LOAD_ACC (LOAD_ACC_out, and_9_out, ALUEN_out);
  not not_3 (not_3_out, Opcode32);
  or u_FLAGEN (FLAGEN_out, FLAG_SET_out, FLAG_RST_out, FLAG_ALU_out);
  nor nor_1 (nor_1_out, not_3_out, T0, T1, T2);
  Priority_Encoder priority_encoder_1 (
    .in0(ALU_ADD_2_sCOMP_out), .in1(ALU_SEB_SHR_out), .in2(ALU_AND_SHL_out), .in3(ALU_OR_INC_out),
    .in4(ALU_XOR_DEC_out), .in5(ALU_MULT_out), .in6(ALU_COMPARE_out), .out(priority_encoder_1_out));  // open: in7, en_in, gs, en_out
  not FFUNCT (FFUNCT_out, nor_1_out);
  Priority_Encoder #(.select(4)) priority_encoder_2 (
    .in0(BUS_MEM_out), .in1(BUS_IR_out), .in2(BUS_AR_out), .in3(BUS_PC_out), .in4(BUS_DR_out),
    .in5(BUS_ACC_out), .in6(BUS_TOS_out), .in7(BUS_CARRY_out), .in8(BUS_FLAG_out), .in9(BUS_3FF_out),
    .out(priority_encoder_2_out));  // open: in10, in11, in12, in13, in14, in15, gs, en_out, en_in
  Priority_Encoder #(.disabled(0)) priority_encoder_3 (
    .in0(LOAD_MEM_out), .in1(LOAD_IR_out), .in2(LOAD_AR_out), .in3(LOAD_PC_out), .in4(LOAD_DR_out),
    .in5(LOAD_ACC_out), .out(priority_encoder_3_out), .gs(priority_encoder_3_gs));  // open: in6, in7, en_in, en_out
  assign ALU_OPTYPE = FFUNCT_out ? or_3_out : 1'bz;  // Controlled_Buffer controlled_buffer_1
  assign ALU_INUTTYPE = FFUNCT_out ? or_4_out : 1'bz;  // Controlled_Buffer controlled_buffer_2
  assign SC__0 = FFUNCT_out ? SC__0_out : 1'bz;  // Controlled_Buffer controlled_buffer_3
  assign LOADBUS = FFUNCT_out ? priority_encoder_3_out : 3'bz;  // Controlled_Buffer controlled_buffer_4
  assign LOADENABLE = FFUNCT_out ? priority_encoder_3_gs : 1'bz;  // Controlled_Buffer controlled_buffer_5
  assign ACC_LOAD_FROM_ALU = FFUNCT_out ? ALUEN_out : 1'bz;  // Controlled_Buffer controlled_buffer_6
  assign LOAD_CARRY = FFUNCT_out ? ALUEN_out : 1'bz;  // Controlled_Buffer controlled_buffer_7
  assign INCPC = FFUNCT_out ? T1 : 1'bz;  // Controlled_Buffer controlled_buffer_8
  assign CLRPC = FFUNCT_out ? 1'b0 : 1'bz;  // Controlled_Buffer controlled_buffer_9
  assign DECtos = FFUNCT_out ? or_1_out : 1'bz;  // Controlled_Buffer controlled_buffer_10
  assign INCtos = FFUNCT_out ? or_2_out : 1'bz;  // Controlled_Buffer controlled_buffer_11
  assign CLRACC = FFUNCT_out ? 1'b0 : 1'bz;  // Controlled_Buffer controlled_buffer_12
  assign OUTBUS = FFUNCT_out ? priority_encoder_2_out : 4'bz;  // Controlled_Buffer controlled_buffer_13
  assign ALU = FFUNCT_out ? priority_encoder_1_out : 3'bz;  // Controlled_Buffer controlled_buffer_14
  assign FLAGEN = FFUNCT_out ? FLAGEN_out : 1'bz;  // Controlled_Buffer controlled_buffer_15
  Priority_Encoder #(.select(2)) priority_encoder_4 (
    .in0(FLAG_SET_out), .in1(FLAG_RST_out), .in2(FLAG_ALU_out), .out(priority_encoder_4_out));  // open: in3, gs, en_out, en_in
  assign FLAGVAL = FFUNCT_out ? priority_encoder_4_out : 2'bz;  // Controlled_Buffer controlled_buffer_16
  assign LOADBUS = nor_1_out ? priority_encoder_5_p1 : 3'bz;  // Controlled_Buffer controlled_buffer_17
  assign LOADENABLE = nor_1_out ? priority_encoder_5_p2 : 1'bz;  // Controlled_Buffer controlled_buffer_18
  assign ACC_LOAD_FROM_ALU = nor_1_out ? ALUTOACC_out : 1'bz;  // Controlled_Buffer controlled_buffer_19
  assign LOAD_CARRY = nor_1_out ? ALUTOACC_out : 1'bz;  // Controlled_Buffer controlled_buffer_20
  assign INCPC = nor_1_out ? 1'b0 : 1'bz;  // Controlled_Buffer controlled_buffer_21
  assign CLRPC = nor_1_out ? 1'b0 : 1'bz;  // Controlled_Buffer controlled_buffer_22
  assign DECtos = nor_1_out ? or_6_out : 1'bz;  // Controlled_Buffer controlled_buffer_23
  or or_5 (or_5_out, and_62_out, and_63_out);
  assign INCtos = nor_1_out ? or_5_out : 1'bz;  // Controlled_Buffer controlled_buffer_24
  assign CLRACC = nor_1_out ? CLRACC_out : 1'bz;  // Controlled_Buffer controlled_buffer_25
  assign OUTBUS = nor_1_out ? priority_encoder_8_p1 : 4'bz;  // Controlled_Buffer controlled_buffer_26
  assign ALU = nor_1_out ? priority_encoder_6_p1 : 3'bz;  // Controlled_Buffer controlled_buffer_27
  assign ALU_OPTYPE = nor_1_out ? ALUOPTYPE_out : 1'bz;  // Controlled_Buffer controlled_buffer_28
  assign ALU_INUTTYPE = nor_1_out ? ALUINPTYPE_out : 1'bz;  // Controlled_Buffer controlled_buffer_29
  assign SC__0 = nor_1_out ? or_7_out : 1'bz;  // Controlled_Buffer controlled_buffer_30
  // Priority_Encoder #(.disabled(0)) priority_encoder_5: pin names not known; wires that end beside it: priority_encoder_5_p1, priority_encoder_5_p2, priority_encoder_5_p3, priority_encoder_5_p4, priority_encoder_5_p5
  and and_62 (and_62_out, or_6_out, not_4_out);
  // Priority_Encoder priority_encoder_6: pin names not known; wires that end beside it: priority_encoder_6_p1, priority_encoder_6_p2, priority_encoder_6_p3, priority_encoder_6_p4, priority_encoder_6_p5, priority_encoder_6_p6, priority_encoder_6_p7, priority_encoder_6_p8
  // Priority_Encoder #(.select(2)) priority_encoder_7: pin names not known; wires that end beside it: priority_encoder_7_p1, priority_encoder_7_p2, priority_encoder_7_p3, priority_encoder_7_p4
  assign FLAGVAL = nor_1_out ? priority_encoder_7_p1 : 2'bz;  // Controlled_Buffer controlled_buffer_31
  assign FLAGEN = nor_1_out ? FLAGEN_2_out : 1'bz;  // Controlled_Buffer controlled_buffer_32
  or or_6 (or_6_out, and_69_out, and_70_out);
  not not_4 (not_4_out, and_70_out);
  // Priority_Encoder #(.select(4)) priority_encoder_8: pin names not known; wires that end beside it: priority_encoder_8_p1, priority_encoder_8_p2, priority_encoder_8_p3, priority_encoder_8_p4, priority_encoder_8_p5
  or FLAGEN_2 (FLAGEN_2_out, priority_encoder_7_p4, priority_encoder_7_p3, priority_encoder_7_p2);
  or ALUTOACC (ALUTOACC_out, and_64_out, and_65_out, and_66_out, and_67_out, and_68_out);
  or ALU_ADD_2_sCOMP_2 (priority_encoder_6_p2, and_72_out, 1'b0);
  or ALU_SEB_SHR_2 (priority_encoder_6_p3, and_73_out, 1'b0);
  or ALU_AND_SHL_2 (priority_encoder_6_p4, and_74_out, 1'b0);
  or ALU_OR_INC_2 (priority_encoder_6_p5, and_75_out, 1'b0);
  or ALU_XOR_DEC_2 (priority_encoder_6_p6, and_92_out, 1'b0);
  buf ALU_MULT_2 (priority_encoder_6_p7, 1'b0);  // OR_Gate
  or ALU_COMPARE_2 (priority_encoder_6_p8, and_93_out, 1'b0);
  or or_7 (or_7_out, and_94_out, and_95_out, and_96_out, and_97_out, and_98_out, and_99_out, and_100_out, and_101_out, and_102_out, and_103_out, and_104_out, and_105_out, and_106_out);
  and and_63 (and_63_out, T5, decoder_1_out10);
  buf BUS_ACC_2 (priority_encoder_8_p2, and_89_out);  // OR_Gate
  buf BUS_ACC_3 (priority_encoder_8_p3, and_71_out);  // OR_Gate
  or BUS_TOS_2 (priority_encoder_8_p4, and_90_out, and_91_out);
  buf BUS_3FF_2 (priority_encoder_8_p5, 1'b0);  // OR_Gate
  or ALUOPTYPE (ALUOPTYPE_out, and_76_out, and_77_out, and_78_out, and_79_out, and_80_out);
  buf ALUINPTYPE (ALUINPTYPE_out, 1'b0);  // OR_Gate
  buf FLAG_RST_2 (priority_encoder_7_p2, and_81_out);  // OR_Gate
  buf FLAG_SET_2 (priority_encoder_7_p3, and_82_out);  // OR_Gate
  buf FLAG_ALU_2 (priority_encoder_7_p4, and_83_out);  // OR_Gate
  buf LOAD_MEM_2 (priority_encoder_5_p3, and_84_out);  // OR_Gate
  or LOAD_AR_2 (priority_encoder_5_p4, and_85_out, and_86_out);
  or LOAD_ACC_2 (priority_encoder_5_p5, and_87_out, ALUTOACC_out);
  and and_64 (and_64_out, decoder_1_out0, T3);
  and and_65 (and_65_out, decoder_1_out1, T3);
  and and_66 (and_66_out, T3, decoder_1_out2);
  and and_67 (and_67_out, T3, decoder_1_out3);
  and and_68 (and_68_out, decoder_1_out4, T3);
  and and_69 (and_69_out, T3, decoder_1_out9);
  and and_70 (and_70_out, decoder_1_out11, T3);
  buf u_CLRACC (CLRACC_out, and_88_out);  // OR_Gate
  and and_71 (and_71_out, T5, decoder_1_out9);
  and and_72 (and_72_out, T3, decoder_1_out4);
  and and_73 (and_73_out, decoder_1_out1, T3);
  and and_74 (and_74_out, decoder_1_out0, T3);
  and and_75 (and_75_out, T3, decoder_1_out2);
  and and_76 (and_76_out, decoder_1_out0, T3);
  and and_77 (and_77_out, decoder_1_out1, T3);
  and and_78 (and_78_out, T3, decoder_1_out2);
  and and_79 (and_79_out, T3, decoder_1_out3);
  and and_80 (and_80_out, T3, decoder_1_out4);
  and and_81 (and_81_out, decoder_1_out8, T3);
  and and_82 (and_82_out, decoder_1_out7, T3);
  and and_83 (and_83_out, T3, decoder_1_out5);
  and and_84 (and_84_out, decoder_1_out9, T5);
  and and_85 (and_85_out, T4, decoder_1_out9);
  and and_86 (and_86_out, T3, decoder_1_out10);
  and and_87 (and_87_out, T4, decoder_1_out10);
  and and_88 (and_88_out, T3, decoder_1_out6);
  and and_89 (and_89_out, T4, decoder_1_out10);
  and and_90 (and_90_out, T4, decoder_1_out9);
  and and_91 (and_91_out, T3, decoder_1_out10);
  and and_92 (and_92_out, T3, decoder_1_out3);
  and and_93 (and_93_out, T3, decoder_1_out5);
  and and_94 (and_94_out, decoder_1_out0, T3);
  and and_95 (and_95_out, decoder_1_out1, T3);
  and and_96 (and_96_out, T3, decoder_1_out2);
  and and_97 (and_97_out, T3, decoder_1_out3);
  and and_98 (and_98_out, T3, decoder_1_out4);
  and and_99 (and_99_out, T3, decoder_1_out5);
  and and_100 (and_100_out, T3, decoder_1_out6);
  and and_101 (and_101_out, T3, decoder_1_out7);
  and and_102 (and_102_out, T3, decoder_1_out8);
  and and_103 (and_103_out, T5, decoder_1_out9);
  and and_104 (and_104_out, T5, decoder_1_out10);
  and and_105 (and_105_out, T3, decoder_1_out11);
  and and_106 (and_106_out, T3, HALT);
  Decoder #(.select(5)) decoder_1 (
    .out0(decoder_1_out0), .out1(decoder_1_out1), .out2(decoder_1_out2), .out3(decoder_1_out3),
    .out4(decoder_1_out4), .out5(decoder_1_out5), .out6(decoder_1_out6), .out7(decoder_1_out7),
    .out8(decoder_1_out8), .out9(decoder_1_out9), .out10(decoder_1_out10), .out11(decoder_1_out11),
    .out12(HALT), .out13(decoder_1_out13), .out14(decoder_1_out14), .sel({AR4, AR3, AR2, AR1, AR0}));  // open: out15, out16, out17, out18, out19, out20, out21, out22, out23, out24, out25, out26, out27, out28, out29, out30, out31, en

  // Notes on the sheet:
  //   T0
  //   T2
  //   T1
  //   T5
  //   T3
  //   T6
  //   T4
  //   T15
endmodule

module CPU (
);

  main main_1 ();
endmodule
